// Logisim project itemb.circ as structural Verilog: 1 circuit, main circuit item1b
module item1b (
  input  A,
  input  B,
  input  C,
  output x
);

  wire not_1_out, or_1_out, or_2_out;

  not not_1 (not_1_out, C);
  or or_1 (or_1_out, A, B);
  and and_1 (x, or_1_out, or_2_out);
  or or_2 (or_2_out, B, not_1_out);
endmodule
