// Logisim project itemc.circ as structural Verilog: 1 circuit, main circuit itemc
module itemc (
  input  A,
  input  B,
  input  C,
  input  D,
  output x
);

  wire or_1_out;

  or or_1 (or_1_out, C, D);
  nand nand_1 (x, A, B, or_1_out);
endmodule
