// Logisim project itemd.circ as structural Verilog: 1 circuit, main circuit item1d
module item1d (
  input  A,
  input  B,
  input  C,
  output x
);

  xor odd_parity_1 (x, A, B, C);
endmodule
