// Logisim project itemd2.circ as structural Verilog: 1 circuit, main circuit item1d
module item1d (
  input  A,
  input  B,
  input  C,
  output y
);

  wire and_1_out, and_2_out, and_3_out;

  and and_1 (and_1_out, A, B);
  and and_2 (and_2_out, B, C);
  or or_1 (y, and_1_out, and_2_out, and_3_out);
  and and_3 (and_3_out, A, C);
endmodule
