// Logisim project sistema_ar_condicionado.circ as structural Verilog: 1 circuit, main circuit main
module main (
  input  F,
  input  U,
  input  T,
  input  H
);

  wire and_1_out, and_2_out, or_1_out;

  and and_1 (and_1_out, F, U);
  and and_2 (and_2_out, T, H);
  or or_1 (or_1_out, and_1_out, and_2_out);
  LED led_1 (.in(or_1_out));
endmodule
